# Fritzing sketch pump Sketch (saved by Fritzing 1.0.0rc)
breadboards: 1

parts:
  WATER_PUMP_12v = water pump/motor
  12_V_Power_Supply = 2.1mm Barrel Jack with Terminal Block
  Liquid_Level_Sensor_Switch = Reed switch [package=THT]
  R5 = Resistor [tolerance=±5% power=0.25 resistance=1k package=THT]
  Liquid_Level_Sensor_Switch_2 = Reed switch [package=THT]
  R7 = Resistor [tolerance=±5% power=0.25 resistance=1k package=THT]
  12V_to_5V_buck_converter = RioRand LM2596
  Part3 = Adafruit 128x64 OLED FeatherWing [part_number="Adafruit #4650"]  # not connected
  Part4 = IFR520 MOS module [package=THT]
  Part2 = Adafruit Feather ESP32-S2 [part_number="Adafruit #5000"]

nets:
  N1: WATER_PUMP_12v.pin_1, Part4.V-
  N2: WATER_PUMP_12v.pin_2, Part4.V+
  N3: 12_V_Power_Supply.POS, 12V_to_5V_buck_converter.Pin_1, Part4.VIN
  GND: 12_V_Power_Supply.NEG, R5.Pin_1, R7.Pin_1, 12V_to_5V_buck_converter.Pin_2, 12V_to_5V_buck_converter.Pin_4, Part4.GND, Part2.GND, Part2.A2
  N4: Liquid_Level_Sensor_Switch.pin_2, Liquid_Level_Sensor_Switch_2.pin_1, Part2.3.3V
  N5: Liquid_Level_Sensor_Switch_2.pin_2, Part2.D5
  N6: 12V_to_5V_buck_converter.Pin_3, Part2.VBUS
  N7: Part4.SIG, Part2.D12

notes:
  black - ground
  red - 12 v
  orange - 5v (powers feather)
  green - 3.3v
  resistor - 1k

custom parts:
  water pump/motor: WATER PUMP BY ARDUBLOCKTR
  Adafruit 128x64 OLED FeatherWing: A Feather board without ambition is a Feather board without FeatherWings! This is the FeatherWing 128x64 OLED: it adds a gorgeous 128x64 monochrome OLED plus 3 user buttons to any Feather main board. Using our Feather Stacking Headers or Feather Female Headers you can connect a FeatherWing on top of your Feather board and let the board take flight! These displays are small, only about 1.3"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
  Adafruit Feather ESP32-S2: What's Feather-shaped and has an ESP32-S2 WiFi module? What has a STEMMA QT connector for I2C devices and a built in ambient sensor? What has your favorite Espressif WiFi microcontroller and lots of Flash and RAM memory for your next IoT project? What will make your next IoT project sensor project flyyyyy? That's right - it's the new Adafruit ESP32-S2 Feather and Adafruit ESP32-S2 Feather with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
