# Fritzing sketch test_pump_Sketch (saved by Fritzing 1.0.0rc)
breadboards: 1

parts:
  R5 = Resistor [tolerance=±5% power=0.25 resistance=1k package=THT]
  Part3 = Adafruit 128x64 OLED FeatherWing [part_number="Adafruit #4650"]  # not connected
  Part2 = Adafruit Feather ESP32-S2 [part_number="Adafruit #5000"]
  U1 = SWITCH_SPDT [package=kps-1290]
  U2 = SWITCH_SPDT [package=kps-1290]
  LED2 = LED - 3mm [color="Blue (430nm)" current=0.030A package="3 mm [THT]"]
  LED3 = LED - 3mm [color="Green (555nm)" current=0.030A package="3 mm [THT]"]
  R6 = Resistor [tolerance=±5% power=0.25 resistance=1k package=THT]
  LED4 = LED - 3mm [color="Red (660nm)" current=0.030A package="3 mm [THT]"]

nets:
  N1: R5.Pin_0, Part2.GND, Part2.A2, LED2.cathode, LED3.anode, R6.Pin_1, LED4.anode
  N2: R5.Pin_1, U1.P
  N3: Part2.D12, LED4.cathode
  N4: Part2.D11, U1.O, LED3.cathode
  N5: Part2.D10, U2.O, LED2.anode
  N6: U2.P, R6.Pin_0

custom parts:
  Adafruit 128x64 OLED FeatherWing: A Feather board without ambition is a Feather board without FeatherWings! This is the FeatherWing 128x64 OLED: it adds a gorgeous 128x64 monochrome OLED plus 3 user buttons to any Feather main board. Using our Feather Stacking Headers or Feather Female Headers you can connect a FeatherWing on top of your Feather board and let the board take flight! These displays are small, only about 1.3"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
  Adafruit Feather ESP32-S2: What's Feather-shaped and has an ESP32-S2 WiFi module? What has a STEMMA QT connector for I2C devices and a built in ambient sensor? What has your favorite Espressif WiFi microcontroller and lots of Flash and RAM memory for your next IoT project? What will make your next IoT project sensor project flyyyyy? That's right - it's the new Adafruit ESP32-S2 Feather and Adafruit ESP32-S2 Feather with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
